// Logisim project ULA.circ as structural Verilog: 1 circuit, main circuit main
module main (
  input  [31:0] VA,
  input  [31:0] VB,
  input  [3:0] in_3,
  output [31:0] out_4
);

  wire comparator_1_lt;
  wire [4:0] bit_extender_1_out, bit_extender_2_out, bit_extender_3_out;
  wire [31:0] adder_1_out, and_1_out, multiplexer_1_out, nor_1_out, or_1_out, shifter_1_out, shifter_2_out,
       shifter_3_out, subtractor_1_out, xor_1_out;

  Bit_Extender #(.in_width(32), .out_width(5)) bit_extender_1 (.in(VB), .out(bit_extender_1_out));
  Bit_Extender #(.in_width(32), .out_width(5)) bit_extender_2 (.in(VB), .out(bit_extender_2_out));
  Bit_Extender #(.in_width(32), .out_width(5)) bit_extender_3 (.in(VB), .out(bit_extender_3_out));
  Adder #(.width(32)) adder_1 (.a(VA), .b(VB), .out(adder_1_out));  // open: cin, cout
  Subtractor #(.width(32)) subtractor_1 (.a(VA), .b(VB), .out(subtractor_1_out));  // open: bin, bout
  assign and_1_out = VA & VB;  // AND_Gate and_1, 32 bits wide
  assign or_1_out = VA | VB;  // OR_Gate or_1, 32 bits wide
  assign xor_1_out = VA ^ VB;  // XOR_Gate xor_1, 32 bits wide
  assign nor_1_out = ~(VA | VB);  // NOR_Gate nor_1, 32 bits wide
  Comparator #(.width(32)) comparator_1 (.a(VA), .b(VB), .lt(comparator_1_lt));  // open: gt, eq
  Shifter #(.width(32)) shifter_1 (.in(VA), .\dist (bit_extender_1_out), .out(shifter_1_out));
  Shifter #(.width(32), .shift("lr")) shifter_2 (.in(VA), .\dist (bit_extender_2_out), .out(shifter_2_out));
  Shifter #(.width(32), .shift("ar")) shifter_3 (.in(VA), .\dist (bit_extender_3_out), .out(shifter_3_out));
  Multiplexer #(.width(32)) multiplexer_1 (
    .in0({32{1'b0}}), .in1(32'h1), .out(multiplexer_1_out), .sel(comparator_1_lt));  // open: en
  Multiplexer #(.select(4), .width(32)) multiplexer_2 (
    .in0(adder_1_out), .in1(subtractor_1_out), .in2(and_1_out), .in3(or_1_out), .in4(xor_1_out),
    .in5(nor_1_out), .in6(multiplexer_1_out), .in7(shifter_1_out), .in8(shifter_2_out), .in9(shifter_3_out),
    .out(out_4), .sel(in_3));  // open: in10, in11, in12, in13, in14, in15, en
endmodule
