// Logisim project separador.circ as structural Verilog: 1 circuit, main circuit main
module main (
  input  [31:0] in_1,
  output [25:0] out_2,
  output [15:0] out_3,
  output [5:0] out_4,
  output [4:0] out_5,
  output [4:0] out_6,
  output [4:0] out_7,
  output [4:0] out_8,
  output [5:0] out_9
);


  assign out_2 = in_1[25:0];
  assign out_3 = in_1[15:0];
  assign out_4 = in_1[5:0];
  assign out_5 = in_1[10:6];
  assign out_6 = in_1[15:11];
  assign out_7 = in_1[20:16];
  assign out_8 = in_1[25:21];
  assign out_9 = in_1[31:26];
endmodule
